# Fritzing sketch Joystick_ProMicro (saved by Fritzing 0.9.3b)
breadboards: 1

parts:
  Часть12 = Arduino Pro Micro (Clone)
  R4 = Rotary Potentiometer (Small) [maximum_resistance=100kΩ package=THT]
  S7 = Toggle Switch [package=THT]
  Часть13 = Thumb Joystick
  IC2 = DIP - 8 pins [chip_label=NRF package="DIP (Dual Inline) [THT]"]

nets:
  GND: Часть12.GND, R4.leg2, S7.L2, Часть13.GND, IC2.GND
  N1: Часть12.D4, Часть13.SEL
  N2: Часть12.D6, S7.COM
  N3: Часть12.A0, Часть13.HORZ
  N4: Часть12.A1, Часть13.VERT
  N5: Часть12.A2, R4.leg1
  VCC: Часть12.VCC, R4.wiper, S7.L1, Часть13.VCC, IC2.VCC

custom parts:
  DIP - 8 pins: A DIP stand-in part for whatever IC you want. With 8 pins on a 300mil dual inline package (DIP) footprint.
